# Fritzing sketch insole (saved by Fritzing 0.9.3b)
circuit board: 8.46667cm x 5.64444cm
breadboards: 1

parts:
  U1 = LuaNode32 / ESP32 [part_number=ESP32S-PIN30]
  J1 = Basic Force Sensing Resistor (FSR) [package=THT]
  J2 = Basic Force Sensing Resistor (FSR) [package=THT]
  J3 = Basic Force Sensing Resistor (FSR) [package=THT]
  J4 = Basic Force Sensing Resistor (FSR) [package=THT]
  J5 = Basic Force Sensing Resistor (FSR) [package=THT]
  R1 = Resistor [tolerance=±5% resistance=10k package="1206 [SMD]"]
  R2 = Resistor [tolerance=±5% resistance=10k package="1206 [SMD]"]
  R3 = Resistor [tolerance=±10% resistance=10k package="1206 [SMD]"]
  R4 = Resistor [tolerance=±10% resistance=10k package="1206 [SMD]"]
  R5 = Resistor [tolerance=±5% resistance=10k package="1206 [SMD]"]
  BAT1 = Battery Holders [package=lipo-1100mAh]

nets (from the breadboard view):
  N1: U1.VP, J5.pin_1, R1.Pin_0
  N2: U1.VN, J4.pin_1, R2.Pin_0
  N3: U1.D34, J3.pin_1, R5.Pin_0
  N4: U1.D35, J2.pin_1, R3.Pin_0
  N5: U1.D32, J1.pin_1
  N6: U1.D25, R4.Pin_0
  N7: U1.GND, J1.pin_0, J2.pin_0, J3.pin_0, J4.pin_0, J5.pin_0, BAT1.-
  N8: U1.Vin, R1.Pin_1, R2.Pin_1, R3.Pin_1, R4.Pin_1, R5.Pin_1, BAT1.+

custom parts:
  LuaNode32 / ESP32: New Image for LuaNode32 DOIT ESP32 DEVKIT V1. Base parts from LuaNode32 / ESP32 ESP32 based LuaNode32 by G.Noorlander DOIT Esp32 DevKit v1 (30 pins long, 11 pins width) by Werner Rothschopf (modified by vanepp Dec 2018)
